# Fritzing sketch radio-rando (saved by Fritzing 0.9.6b)
breadboards: 1

parts:
  Raspberry_Pi1 = Raspberry Pi B+
  S1 = Pushbutton [package="[THT]"]
  RE1 = Rotary Encoder [package=THT]
  Part1 = Adafruit MAX98357A I2S 3W Class D Amplifier [part_number="Adafruit #3006"]

nets:
  N1: Raspberry_Pi1.GPIO4, S1.Pin_1, S1.Pin_2
  GND: Raspberry_Pi1.GND, S1.Pin_3, S1.Pin_4, RE1.EncoderPinC, Part1.GND
  N2: Raspberry_Pi1.GPIO19, Part1.LRCLK
  N3: Raspberry_Pi1.GPIO21, Part1.DIN
  N4: Raspberry_Pi1.GPIO24, RE1.EncoderPinB
  N5: Raspberry_Pi1.GPIO23, RE1.EncoderPinA
  N6: Raspberry_Pi1.GPIO18, Part1.BCLK
  5V: Raspberry_Pi1.5V, Part1.VIN

notes:
  on mine this is a button too

custom parts:
  Adafruit MAX98357A I2S 3W Class D Amplifier: Listen to this good news - we now have an all in one digital audio amp breakout board that works incredibly well with the Raspberry Pi! If you're looking for an easy and low cost way to get you digital sound files bumpin' then the MAX08357 I2S Amp Breakout is for you. It takes standard I2S digital audio input and, not only decodes it into analog, but also amplifies it directly into a speaker.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
